// Digital circuit CPU.dig as structural Verilog
module CPU (
  input  CLK,
  input  RegF_WE,
  input  [7:0] in_8bits,
  input  in_15,
  input  in_16,
  input  in_17,
  output [7:0] out_8bits,
  output [7:0] ddd,
  output [7:0] out_6,
  output [2:0] out_7,
  output [7:0] out_8,
  output [7:0] out_9,
  output [7:0] out_10,
  output [7:0] out_11,
  output [7:0] out_12,
  output [7:0] out_13,
  output [7:0] out_14,
  output [11:0] out_18,
  output [11:0] out_19,
  output [11:0] out_20
);

  wire and_1_out, and_2_out, and_3_out, and_4_out, and_5_out, and_6_out, Branching_SetUp_q, CLK_t,
       comparator_1_eq, comparator_2_eq, counterpreset_1_ovf, EX_IMM_check, EX_Jump_do, EX_Jump_en,
       EX_Math_en, EX_Mem_en, EX_Mov_en, EX_NO_NOP, EX_NOP_out, Go_Branch, ID_IMM_check, ME_DelayNOP,
       ME_do_input, ME_do_output, ME_Mem_doLD, ME_Mem_doSTR, multiplexer_3_out, multiplexer_12_out,
       not_1_out, not_2_out, not_3_out, not_4_out, not_5_out, not_6_out, not_7_out, NotNOPing, or_2_out,
       or_3_out, or_4_out, register_4_q, register_5_q, register_6_q, register_7_q, register_8_q, WB_EN,
       WB_NO_NOP;
  wire [1:0] counter_1_out, EX_Do_SMTH;
  wire [2:0] EX_R_Dest, EX_R_Src1, EX_R_Src2, EX_SMTH_Choice, ID_R_Dest, ID_R_Src1, ID_R_Src2, ME_R_DestOut,
       ME_R_Src2, multiplexer_10_out, register_1_q;
  wire [3:0] ALU_c_f, EX_Reg_F, ID_Opcode;
  wire [4:0] rom_1_d;
  wire [7:0] EX_ALU_Out, EX_Data_A, EX_Data_B, EX_Forward_A, EX_Forward_B, ID_Data_A, ID_Data_B,
       ME_LD_ST_output, ME_RD_WR_output, multiplexer_1_out, multiplexer_2_out, multiplexer_9_out,
       multiplexer_15_out, R_Src_2_Out, register_2_q;
  wire [7:3] ID_R_Src2_IMM;
  wire [11:11] multiplexer_13_out, or_5_out;
  wire [15:0] EX_ME_Forward_out, register_3_q;
  wire [19:0] Instruction_d;
  wire [19:19] IF_ID_q, multiplexer_4_out, multiplexer_6_out;
  wire [25:0] EX_ME_out, multiplexer_16_out, register_9_q;
  wire [31:31] multiplexer_14_out;

  or or_1 (CLK_t, CLK, in_17, in_16, in_15);
  CounterPreset #(.Bits(8)) counterpreset_1 (
    .en(NotNOPing), .C(CLK_t), .dir(1'b0), .in(EX_Data_B), .ld(Go_Branch), .clr(counterpreset_1_ovf),
    .out(ddd), .ovf(counterpreset_1_ovf));
  nand nand_1 (NotNOPing, not_1_out, or_3_out);
  or or_2 (or_2_out, Go_Branch, comparator_1_eq);
  or or_3 (or_3_out, multiplexer_3_out, Go_Branch);
  Register Branching_SetUp (.D(or_3_out), .C(CLK_t), .en(or_2_out), .Q(Branching_SetUp_q));
  and and_1 (and_1_out, CLK_t, EX_NO_NOP);
  Register #(.Bits(3)) register_1 (.D(EX_ME_out[18:16]), .C(CLK_t), .en(1'b1), .Q(register_1_q));
  Multiplexer #(.Bits(8)) multiplexer_1 (
    .sel(ME_do_input), .in_0(R_Src_2_Out), .in_1(in_8bits), .out(multiplexer_1_out));
  Counter #(.Bits(2)) counter_1 (
    .en(Branching_SetUp_q), .C(CLK_t), .clr(comparator_1_eq), .out(counter_1_out));  // open: ovf
  Demultiplexer #(.Selector_Bits(2)) demultiplexer_1 (
    .sel(EX_Do_SMTH), .in(EX_NO_NOP), .out_0(EX_Math_en), .out_1(EX_Mem_en), .out_2(EX_Jump_en),
    .out_3(EX_Mov_en));
  Demultiplexer #(.Bits(3)) demultiplexer_2 (
    .sel(ME_do_output), .in(register_1_q), .out_0(ME_R_DestOut), .out_1(ME_R_Src2));
  Multiplexer #(.Bits(8)) multiplexer_2 (.sel(EX_Mov_en), .in_0(EX_ALU_Out), .in_1(EX_Data_B), .out(multiplexer_2_out));
  Register #(.Bits(8)) register_2 (.D(multiplexer_1_out), .C(CLK_t), .en(EX_ME_out[24]), .Q(register_2_q));
  ROM #(.AddrBits(8), .Bits(20)) Instruction (.A(ddd), .sel(NotNOPing), .D(Instruction_d));
  Multiplexer multiplexer_3 (.sel(comparator_1_eq), .in_0(Branching_SetUp_q), .in_1(1'b0), .out(multiplexer_3_out));
  Comparator #(.Bits(2)) comparator_1 (.a(counter_1_out), .b(2'b10), .eq(comparator_1_eq));  // open: gt, lt
  Demultiplexer #(.Bits(8)) demultiplexer_3 (
    .sel(ME_do_input), .in(register_2_q), .out_0(out_8bits), .out_1(ME_RD_WR_output));
  not not_1 (not_1_out, comparator_1_eq);
  forward_register forward_register_1 (
    .Data_PostEX(multiplexer_2_out), .R_Dest_In(EX_R_Dest), .Do_SMTH(EX_Do_SMTH), .CLK(and_1_out),
    .Data_1(EX_Data_A), .Data_2(EX_Data_B), .R_Src1(EX_R_Src1), .R_Src2(EX_R_Src2), .IMM_Check(EX_IMM_check),
    .Out_1(EX_Forward_A), .Out_2(EX_Forward_B), .DBG1(out_18), .DBG2(out_19), .DBG3(out_20));
  Demultiplexer #(.Selector_Bits(2)) demultiplexer_4 (
    .sel(EX_ME_out[20:19]), .in(EX_ME_out[24]), .out_0(ME_Mem_doLD), .out_1(ME_Mem_doSTR),
    .out_2(ME_do_output), .out_3(ME_do_input));
  Register #(.Bits(16)) register_3 (.D(EX_ME_Forward_out), .C(CLK_t), .en(1'b1), .Q(register_3_q));
  Multiplexer multiplexer_4 (.sel(NotNOPing), .in_0(1'b0), .in_1(Instruction_d[19]), .out(multiplexer_4_out[19]));
  Register register_4 (.D(EX_ME_out[25]), .C(CLK_t), .en(1'b1), .Q(register_4_q));
  not not_2 (not_2_out, EX_Jump_do);
  not not_3 (not_3_out, EX_ME_out[20]);
  Register register_5 (.D(not_2_out), .C(CLK_t), .en(1'b1), .Q(register_5_q));
  RAMDualPort #(.AddrBits(8), .Bits(8)) ramdualport_1 (
    .A(register_3_q[15:8]), .Din(register_3_q[7:0]), .str(ME_Mem_doSTR), .C(and_2_out), .ld(ME_Mem_doLD),
    .D(ME_LD_ST_output));
  and and_2 (and_2_out, CLK_t, not_3_out);
  Multiplexer multiplexer_5 (.sel(or_4_out), .in_0(EX_ME_out[25]), .in_1(register_4_q), .out(ME_DelayNOP));
  or or_4 (or_4_out, register_5_q, register_6_q);
  Register register_6 (.D(register_5_q), .C(CLK_t), .en(1'b1), .Q(register_6_q));
  Register #(.Bits(20)) IF_ID (
    .D({multiplexer_4_out[19], Instruction_d[18:0]}), .C(CLK_t), .en(1'b1),
    .Q({IF_ID_q[19], ID_IMM_check, ID_Opcode, ID_R_Dest, ID_R_Src1, ID_R_Src2_IMM, ID_R_Src2}));
  Register register_7 (.D(EX_ME_out[24]), .C(CLK_t), .en(1'b1), .Q(register_7_q));
  Multiplexer multiplexer_6 (.sel(NotNOPing), .in_0(1'b0), .in_1(IF_ID_q[19]), .out(multiplexer_6_out[19]));
  and and_3 (and_3_out, EX_Jump_en, EX_NO_NOP);
  and and_4 (and_4_out, EX_Math_en, EX_NO_NOP);
  Multiplexer multiplexer_7 (.sel(and_3_out), .in_0(1'b0), .in_1(EX_Jump_do), .out(Go_Branch));
  Register register_8 (.D(EX_ME_out[24]), .C(CLK_t), .en(1'b1), .Q(register_8_q));
  ALU ALU (
    .A(EX_Forward_A), .B(EX_Forward_B), .Do_Math(EX_SMTH_Choice), .Res(EX_ALU_Out), .C_F(ALU_c_f[0]),
    .O_F(ALU_c_f[1]), .N_F(ALU_c_f[2]), .Z_F(ALU_c_f[3]));
  Multiplexer #(.Selector_Bits(2)) multiplexer_8 (
    .sel(EX_SMTH_Choice[1:0]), .in_0(EX_Reg_F[0]), .in_1(EX_Reg_F[3]), .in_2(not_4_out), .in_3(1'b1),
    .out(EX_Jump_do));
  not not_4 (not_4_out, EX_Reg_F[3]);
  Register #(.Bits(26)) register_9 (.D(EX_ME_out), .C(CLK_t), .en(1'b1), .Q(register_9_q));
  and and_5 (and_5_out, WB_NO_NOP, 1'b1, RegF_WE);
  not not_5 (not_5_out, EX_Jump_do);
  Multiplexer #(.Bits(8)) multiplexer_9 (
    .sel(EX_ME_out[20]), .in_0(ME_LD_ST_output), .in_1(ME_RD_WR_output), .out(multiplexer_9_out));
  or or_5 (or_5_out[11], register_9_q[25], ME_DelayNOP);
  Multiplexer #(.Bits(3)) multiplexer_10 (
    .sel(register_7_q), .in_0(ID_R_Src2), .in_1(ME_R_Src2), .out(multiplexer_10_out));
  ROM #(.AddrBits(4), .Bits(5)) rom_1 (.A(ID_Opcode), .sel(1'b1), .D(rom_1_d));
  not not_6 (not_6_out, EX_NO_NOP);
  and and_6 (and_6_out, not_5_out, and_3_out);
  or or_6 (WB_EN, register_8_q, ME_DelayNOP);
  Multiplexer #(.Bits(8)) multiplexer_11 (
    .sel(ID_IMM_check), .in_0(R_Src_2_Out), .in_1({ID_R_Src2_IMM, ID_R_Src2}), .out(ID_Data_B));
  Multiplexer multiplexer_12 (.sel(and_6_out), .in_0(not_6_out), .in_1(1'b1), .out(multiplexer_12_out));
  Multiplexer #(.Bits(12)) multiplexer_13 (
    .sel(not_7_out), .in_0({ME_DelayNOP, ME_R_DestOut, multiplexer_9_out}),
    .in_1({or_5_out[11], ME_R_DestOut, register_9_q[7:0]}), .out({multiplexer_13_out[11], out_7, out_6}));
  RegisterFile #(.AddrBits(3), .Bits(8)) RegFile (
    .Din(out_6), .we(and_5_out), .Rw(out_7), .C(CLK_t), .Ra(ID_R_Src1), .Rb(multiplexer_10_out),
    .Da(ID_Data_A), .Db(R_Src_2_Out));
  Register #(.Bits(4)) register_10 (.D(ALU_c_f), .C(CLK_t), .en(and_4_out), .Q(EX_Reg_F));
  or or_7 (EX_NOP_out, Go_Branch, multiplexer_12_out);
  not not_7 (not_7_out, WB_EN);
  Multiplexer multiplexer_14 (.sel(NotNOPing), .in_0(1'b0), .in_1(multiplexer_6_out[19]), .out(multiplexer_14_out[31]));
  Register #(.Bits(16)) EX_ME_Forward (.D({EX_Forward_B, EX_Forward_A}), .C(CLK_t), .en(1'b1), .Q(EX_ME_Forward_out));
  Register #(.Bits(32)) ID_EX (
    .D({multiplexer_14_out[31], ID_IMM_check, ID_R_Src2, ID_R_Src1, rom_1_d, ID_R_Dest, ID_Data_A, ID_Data_B}),
    .C(CLK_t), .en(1'b1),
    .Q({EX_NO_NOP, EX_IMM_check, EX_R_Src2, EX_R_Src1, EX_Do_SMTH, EX_SMTH_Choice, EX_R_Dest, EX_Data_A, EX_Data_B}));
  Register #(.Bits(26)) EX_ME (.D(multiplexer_16_out), .C(CLK_t), .en(1'b1), .Q(EX_ME_out));
  not not_8 (WB_NO_NOP, multiplexer_13_out[11]);
  Multiplexer #(.Selector_Bits(2), .Bits(8)) multiplexer_15 (
    .sel(EX_Do_SMTH), .in_0(EX_ALU_Out), .in_1({8{1'b0}}), .in_2({8{1'b0}}), .in_3(EX_Data_B),
    .out(multiplexer_15_out));
  Comparator #(.Bits(2)) comparator_2 (.a(EX_Do_SMTH), .b(2'b01), .eq(comparator_2_eq));  // open: gt, lt
  Multiplexer #(.Bits(26)) multiplexer_16 (
    .sel(comparator_2_eq),
    .in_0({EX_NOP_out, 1'b0, EX_Do_SMTH, EX_SMTH_Choice, EX_R_Dest, {8{1'b0}}, multiplexer_15_out}),
    .in_1({EX_NOP_out, 1'b1, EX_Do_SMTH, EX_SMTH_Choice, EX_R_Dest, EX_Data_A, EX_Data_B}),
    .out(multiplexer_16_out));

  assign out_8 = ddd;
  assign out_9 = ddd;
  assign out_10 = ddd;
  assign out_11 = ddd;
  assign out_12 = ddd;
  assign out_13 = ddd;
  assign out_14 = ddd;

  // Other names for the same wires on the sheet: ID_R_Src2_IMM[2:0] = ID_R_Src2; WB_output[7:0] = out_6;
  //   WB_R_Dest[2:0] = out_7; CLK_Lower = in_15; CLK_Middle = in_16; CLK_Upper = in_17;
  //   ME_Data_B[7:0] = EX_ME_out[7:0]; ME_Data_A[7:0] = EX_ME_out[15:8]; ME_R_Dest[2:0] = EX_ME_out[18:16];
  //   ME_SMTH_Choice[2:0] = EX_ME_out[21:19]; ME_Do_choice = EX_ME_out[20]; ME_Do_smth[1:0] = EX_ME_out[23:22];
  //   ME_EN = EX_ME_out[24]; ME_NOP = EX_ME_out[25]; RegF_C = EX_Reg_F[0]; RegF_O = EX_Reg_F[1]; RegF_N = EX_Reg_F[2];
  //   RegF_Z = EX_Reg_F[3]; EX_MOV_Out[7:0] = EX_Data_B;
  //   ID_EX[31:0] = {EX_NO_NOP, EX_IMM_check, EX_R_Src2, EX_R_Src1, EX_Do_SMTH, EX_SMTH_Choice, EX_R_Dest, EX_Data_A, EX_Data_B};
  //   Line_Branch[7:0] = EX_Data_B; in_8bit[7:0] = in_8bits; PC_Out[7:0] = ddd

  // Notes on the sheet:
  //   RegF_WE: default 1
  //   Opcode
  //   0000: LD
  //   0001: MOV
  //   0010: ST
  //   0011: RD
  //   0100: ADD
  //   0101L SUB
  //   0110: MUL
  //   0111: WR
  //   1000: AND
  //   1001: OR
  //   1010: XOR
  //   1011: NOT
  //   1100: BC
  //   1101:BZ
  //   1110: BNZ
  //   1111:B
  //   Pipeline Stages
  //   Instruction Fetch
  //   Execute
  //   Memory
  //   Branch Prediction
  //   Static Guess Not Taken Branch
  //   Do_{RD/WR}
  //   Might be problem here
  //   Sol: change to 2 bits
  //   and detect for 10
  //   contents of Instruction (hex, n*v repeats v):
  //   c4011,c482f,91100,95900,c8364,c0864,da105,ae804,a3504,d6464,f8009,c78ff
  //   IF/ID
  //   Do_{LD/ST}
  //   PC_{Out}
  //   Instruction Decode
  //   Do_{Math}
  //   Do_{Jump}
  //   ME/WB
  //   CU
  //   Do_{SMTH}: 4:3
  //   00 Do_{Math}(In:EX -> WB)
  //   01 Do_{Mem} (In:EX -> ME)
  //   10 Do_{Jump} (IMM only) (In:Somewhere)
  //   11 Do_{Mov} (IMM only) (In:EX)
  //   SMTH_{Choice}: 2:0
  //   contents of rom_1 (hex, n*v repeats v):
  //   8,18,9,b,0,1,2,a,4,5,6,7,10,11,12,13
  //   Write Back
  //   EX/ME
  //   ID/EX
endmodule
